# Fritzing sketch aipod (saved by Fritzing 0.9.3b)
breadboards: 1

parts:
  LCD1 = LCD screen
  S1 = Pushbutton [package="[THT]"]
  Raspberry_Pi_1 = Raspberry Pi 3 [part_number=RPI-3-V1.2]
  S2 = Pushbutton [package="[THT]"]

nets:
  VSS: LCD1.VSS, LCD1.V0, LCD1.R/W, LCD1.LED-, S1.Pin_3, S1.Pin_4, Raspberry_Pi_1.GND, S2.Pin_3, S2.Pin_4
  VDD: LCD1.VDD, LCD1.LED+, Raspberry_Pi_1.5V
  N1: LCD1.RS, Raspberry_Pi_1.GIPO16
  N2: LCD1.E, Raspberry_Pi_1.GIPO12
  N3: LCD1.DB4, Raspberry_Pi_1.GIPO25
  N4: LCD1.DB5, Raspberry_Pi_1.GIPO24
  N5: LCD1.DB6, Raspberry_Pi_1.GIPO23
  N6: LCD1.DB7, Raspberry_Pi_1.GIPO18
  N7: S1.Pin_1, S1.Pin_2, Raspberry_Pi_1.GIPO4
  N8: S2.Pin_1, S2.Pin_2
